// Logisim project Adder.circ as structural Verilog: 3 circuits, main circuit 半加器自动生成
module \半加器自动生成  (
  input  A,
  input  B,
  output Co,
  output S
);

  wire and_2_out, and_3_out, not_1_out, not_2_out;

  and and_1 (Co, A, B);
  not not_1 (not_1_out, A);
  not not_2 (not_2_out, B);
  and and_2 (and_2_out, not_1_out, B);
  and and_3 (and_3_out, A, not_2_out);
  or or_1 (S, and_2_out, and_3_out);
endmodule

// FA
module \手绘全加器  (
  input  Ai,
  input  Bi,
  input  Cin,
  output Si,
  output Cout
);

  wire and_1_out, and_2_out, and_3_out, and_4_out, and_5_out, and_6_out, and_7_out, not_1_out, not_2_out,
       not_3_out, not_4_out, not_5_out, not_6_out;

  and and_1 (and_1_out, Bi, Cin);
  and and_2 (and_2_out, Ai, Cin);
  and and_3 (and_3_out, Ai, Bi);
  not not_1 (not_1_out, Ai);
  not not_2 (not_2_out, Bi);
  not not_3 (not_3_out, Ai);
  not not_4 (not_4_out, Cin);
  not not_5 (not_5_out, Bi);
  not not_6 (not_6_out, Cin);
  or or_1 (Si, and_1_out, and_2_out, and_3_out);
  and and_4 (and_4_out, not_1_out, not_2_out, Cin);
  and and_5 (and_5_out, not_3_out, Bi, not_4_out);
  and and_6 (and_6_out, Ai, not_5_out, not_6_out);
  and and_7 (and_7_out, Ai, Bi, Cin);
  or or_2 (Cout, and_4_out, and_5_out, and_6_out, and_7_out);
endmodule

// 4位加法
module \_4位行波进位加法器  (
  input  [3:0] X,
  input  [3:0] Y,
  input  Cin,
  output [3:0] Sum,
  output Cout
);

  wire \手绘全加器_2_si , \手绘全加器_3_si , \手绘全加器_4_si ;

  \手绘全加器  \u_手绘全加器_1  (.Ai(\手绘全加器_2_si ), .Bi(X[3]), .Si(Cout), .Cin(Y[3]), .Cout(Sum[3]));
  \手绘全加器  \u_手绘全加器_2  (.Ai(\手绘全加器_3_si ), .Bi(X[2]), .Si(\手绘全加器_2_si ), .Cin(Y[2]), .Cout(Sum[2]));
  \手绘全加器  \u_手绘全加器_3  (.Ai(\手绘全加器_4_si ), .Bi(X[1]), .Si(\手绘全加器_3_si ), .Cin(Y[1]), .Cout(Sum[1]));
  \手绘全加器  \u_手绘全加器_4  (.Ai(Cin), .Bi(X[0]), .Si(\手绘全加器_4_si ), .Cin(Y[0]), .Cout(Sum[0]));
  // Probe on X
  // Probe on Y
  // Probe on Sum
  // Probe on X
  // Probe on Y
  // Probe on Sum

  // Other names for the same wires on the sheet: Ci = Cin; Co = Cout; S[3:0] = Sum; S0 = Sum[0]; S1 = Sum[1];
  //   S2 = Sum[2]; S3 = Sum[3]

  // Notes on the sheet:
  //   Y: pull=down
  //   X: pull=down
  //   Cin: pull=down
  //   输入引脚区
  //   输出引脚区
  //   功能说明:4位串行加法器 S=X+Y+Cin，Cout为最高位进位，Cin为进位输入
  //   +
  //   =
  //   有符号加法
  //   +
  //   =
  //   无符号加法
endmodule
