// Logisim project Adder4Test.circ as structural Verilog: 1 circuit, main circuit Test
module Test (
  output [7:0] Cnt,
  output [3:0] X,
  output [3:0] Y,
  output Co,
  output [3:0] S,
  output _passed,
  output halt
);

  wire CLK, Running;
  wire [3:0] counter_2_q;
  wire [4:0] Rstd;

  Clock #(.highDuration(1), .lowDuration(1)) clock_1 (.out(CLK));
  Counter #(.width(8), .max('hff), .ongoal("wrap"), .trigger("rising"), .behavior("old")) counter_1 (
    .count(Running), .Q(Cnt), .clk(CLK));  // open: load, D, carry, clr, preset
  Counter #(.width(4), .max('hf), .ongoal("wrap"), .trigger("falling"), .behavior("old")) counter_2 (
    .count(Running), .Q(counter_2_q), .clk(Cnt[3]));  // open: load, D, carry, clr, preset
  // Probe on Cnt
  // Probe on Cnt
  // Probe on {8{1'b1}}
  not not_1 (Running, halt);
  Comparator #(.width(8), .mode("twosComplement")) comparator_1 (.a(Cnt), .b({8{1'b1}}), .eq(halt));  // open: gt, lt
  ROM #(.addrWidth(4), .dataWidth(4), .Select("high")) rom_1 (.addr(Cnt[3:0]), .data(Y));
  ROM #(.addrWidth(4), .dataWidth(4), .Select("high")) rom_2 (.addr(counter_2_q), .data(X));
  ROM #(.addrWidth(8), .dataWidth(5), .Select("high")) rom_3 (.addr(Cnt), .data(Rstd));
  \_4位行波进位加法器  \u_4位行波进位加法器_1  (.X(X), .Y(Y), .Sum(S), .Cout(Co));  // open: Cin
  Comparator #(.width(5), .mode("unsigned")) comparator_2 (.a({Co, S}), .b(Rstd), .eq(_passed));  // open: gt, lt
  Pull_Resistor #(.pull(0)) pull_resistor_1 (.node(_passed));
  RAM #(.addrWidth(8), .dataWidth(5), .bus("separate"), .Select("low")) ram_1 (
    .addr(Cnt), .din({Co, S}), .clk(CLK));  // open: data, str, sel, ld, clr

  // Other names for the same wires on the sheet: Equal = _passed; Result[4:0] = {Co, S}; tunnel[7:0] = Cnt

  // Notes on the sheet:
  //   测试节拍数
  //   contents of rom_1 (hex, n*v repeats v):
  //   0 1 2 3 4 5 6 7 8 9 a b c d e f
  //   contents of rom_2 (hex, n*v repeats v):
  //   0 1 2 3 4 5 6 7 8 9 a b c d e f
  //   contents of rom_3 (hex, n*v repeats v):
  //   0 1 2 3 4 5 6 7 8 9 a b c d e f 1 2 3 4 5 6 7 8 9 a b c d e f 10 2 3 4 5 6 7 8 9 a b c d e f 10 11 3
  //   4 5 6 7 8 9 a b c d e f 10 11 12 4 5 6 7 8 9 a b c d e f 10 11 12 13 5 6 7 8 9 a b c d e f 10 11 12
  //   13 14 6 7 8 9 a b c d e f 10 11 12 13 14 15 7 8 9 a b c d e f 10 11 12 13 14 15 16 8 9 a b c d e f
  //   10 11 12 13 14 15 16 17 9 a b c d e f 10 11 12 13 14 15 16 17 18 a b c d e f 10 11 12 13 14 15 16 17
  //   18 19 b c d e f 10 11 12 13 14 15 16 17 18 19 1a c d e f 10 11 12 13 14 15 16 17 18 19 1a 1b d e f
  //   10 11 12 13 14 15 16 17 18 19 1a 1b 1c e f 10 11 12 13 14 15 16 17 18 19 1a 1b 1c 1d f 10 11 12 13
  //   14 15 16 17 18 19 1a 1b 1c 1d 1e
endmodule
