// Logisim project HATest.circ as structural Verilog: 1 circuit, main circuit Test
module Test (
  output [3:0] Cnt,
  output [1:0] AB,
  output Co,
  output S,
  output _passed,
  output halt
);

  wire CLK, Running;
  wire [1:0] Rstd;

  Clock #(.highDuration(1), .lowDuration(1)) clock_1 (.out(CLK));
  Counter #(.width(4), .max('hf), .ongoal("wrap"), .trigger("rising"), .behavior("old")) counter_1 (
    .count(Running), .Q(Cnt), .clk(CLK));  // open: load, D, carry, clr, preset
  // Probe on Cnt
  // Probe on Cnt
  // Probe on 4'b0011
  Comparator #(.width(4), .mode("twosComplement")) comparator_1 (.a(Cnt), .b(4'b0011), .eq(halt));  // open: gt, lt
  ROM #(.addrWidth(4), .dataWidth(2), .Select("high")) rom_1 (.addr(Cnt), .data(AB));
  ROM #(.addrWidth(4), .dataWidth(2), .Select("high")) rom_2 (.addr(Cnt), .data(Rstd));
  not not_1 (Running, halt);
  RAM #(.addrWidth(4), .dataWidth(2), .bus("separate"), .Select("low")) ram_1 (
    .addr(Cnt), .din({Co, S}), .str(Running), .clk(CLK));  // open: data, sel, ld, clr
  \半加器自动生成  \u_半加器自动生成_1  (.A(AB[0]), .Co(Co), .B(AB[1]), .S(S));
  Comparator #(.width(2), .mode("unsigned")) comparator_2 (.a({Co, S}), .b(Rstd), .eq(_passed));  // open: gt, lt
  Pull_Resistor #(.pull(0)) pull_resistor_1 (.node(_passed));

  // Other names for the same wires on the sheet: Equal = _passed; Result[1:0] = {Co, S}; tunnel[3:0] = Cnt

  // Notes on the sheet:
  //   测试节拍数
  //   contents of rom_1 (hex, n*v repeats v):
  //   0 1 2 3 0 1 2 3
  //   contents of rom_2 (hex, n*v repeats v):
  //   0 1 1 2 0 1 1 2
endmodule
