// Logisim project lab1.1.circ as structural Verilog: 1 circuit, main circuit main
// Truth
module main (
  input  X,
  input  Y,
  input  Z,
  output F
);

  wire nand_1_out, nand_2_out, nand_3_out, nand_4_out, nand_5_out;

  nand nand_1 (nand_1_out, Y, Z);
  nand nand_2 (nand_2_out, X, Z);
  nand nand_3 (nand_3_out, nand_1_out, nand_2_out);
  nand nand_4 (nand_4_out, nand_3_out, nand_3_out);
  nand nand_5 (nand_5_out, X, Y);
  nand nand_6 (F, nand_4_out, nand_5_out);
endmodule
