// Logisim project lab1.4.circ as structural Verilog: 1 circuit, main circuit main
module main (
  input  D0,
  input  D1,
  input  S,
  output Y
);

  wire nand_1_out, nand_2_out, nand_3_out;

  nand nand_1 (nand_1_out, S, S);
  nand nand_2 (nand_2_out, D1, S);
  nand nand_3 (nand_3_out, D0, nand_1_out);
  nand nand_4 (Y, nand_2_out, nand_3_out);
endmodule
