// Logisim project lab3.2.circ as structural Verilog: 2 circuits, main circuit SHRG4U
module SHRG4U (
  input  CLK,
  input  CLR_L,
  input  RIN,
  input  D3,
  input  D2,
  input  D1,
  input  D0,
  input  LIN,
  input  S1,
  input  S0,
  output Q3,
  output Q2,
  output Q1,
  output Q0
);

  wire and_1_out, and_2_out, and_3_out, and_4_out, and_5_out, and_6_out, and_7_out, and_8_out, and_9_out,
       and_10_out, and_11_out, and_12_out, and_13_out, and_14_out, and_15_out, and_16_out, buffer_1_out,
       not_1_out, not_2_out, not_3_out, not_4_out, not_5_out, not_6_out, or_1_out, or_2_out, or_3_out,
       or_4_out;

  not not_1 (not_1_out, S1);
  not not_2 (not_2_out, S0);
  not not_3 (not_3_out, not_1_out);
  not not_4 (not_4_out, not_2_out);
  not not_5 (not_5_out, CLK);
  buf buffer_1 (buffer_1_out, CLR_L);
  not not_6 (not_6_out, buffer_1_out);
  and and_1 (and_1_out, RIN, not_3_out, not_2_out);
  and and_2 (and_2_out, Q3, not_1_out, not_2_out);
  and and_3 (and_3_out, D3, not_3_out, not_4_out);
  and and_4 (and_4_out, Q2, not_1_out, not_4_out);
  and and_5 (and_5_out, Q3, not_3_out, not_2_out);
  and and_6 (and_6_out, Q2, not_1_out, not_2_out);
  and and_7 (and_7_out, D2, not_3_out, not_4_out);
  and and_8 (and_8_out, Q1, not_1_out, not_4_out);
  or or_1 (or_1_out, and_1_out, and_2_out, and_3_out, and_4_out);
  and and_9 (and_9_out, Q2, not_3_out, not_2_out);
  and and_10 (and_10_out, Q1, not_1_out, not_2_out);
  and and_11 (and_11_out, D1, not_3_out, not_4_out);
  and and_12 (and_12_out, Q0, not_1_out, not_4_out);
  and and_13 (and_13_out, Q1, not_3_out, not_2_out);
  and and_14 (and_14_out, Q0, not_1_out, not_2_out);
  and and_15 (and_15_out, D0, not_3_out, not_4_out);
  and and_16 (and_16_out, LIN, not_1_out, not_4_out);
  or or_2 (or_2_out, and_5_out, and_6_out, and_7_out, and_8_out);
  or or_3 (or_3_out, and_9_out, and_10_out, and_11_out, and_12_out);
  or or_4 (or_4_out, and_13_out, and_14_out, and_15_out, and_16_out);
  D_Flip_Flop #(.trigger("falling")) QD (.clk(not_5_out), .D(or_1_out), .Q(Q3), .reset(not_6_out));  // open: Qn, preset
  D_Flip_Flop #(.trigger("falling")) QC (.clk(not_5_out), .D(or_2_out), .Q(Q2), .reset(not_6_out));  // open: Qn, preset
  D_Flip_Flop #(.trigger("falling")) QB (.clk(not_5_out), .D(or_3_out), .Q(Q1), .reset(not_6_out));  // open: Qn, preset
  D_Flip_Flop #(.trigger("falling")) QB_2 (
    .clk(not_5_out), .D(or_4_out), .Q(Q0), .reset(not_6_out));  // open: Qn, preset

  // Notes on the sheet:
  //   输入引脚
  //   请勿修改引脚名称、电路名称及电路封装外观
  //   提示：使用独立逻辑门实现4位异步清零移位寄存器，禁止直接使用移位寄存器组件。
  //   输出引脚
endmodule

module \_8位伪随机数生成器  (
  input  in_1,
  input  CLR_L,
  input  [7:0] in_3,
  input  in_4,
  output [7:0] out_5
);

  wire and_1_out, xor_1_out;
  wire [7:0] multiplexer_1_out;

  Multiplexer #(.width(8), .enable("false")) multiplexer_1 (
    .in0(out_5), .in1(in_3), .out(multiplexer_1_out), .sel(in_4));
  and and_1 (and_1_out, 1'b1, in_4);
  SHRG4U shrg4u_1 (
    .CLK(in_1), .CLR_L(CLR_L), .RIN(and_1_out), .Q3(out_5[3]), .Q2(out_5[2]), .D3(multiplexer_1_out[3]),
    .D2(multiplexer_1_out[2]), .D1(multiplexer_1_out[1]), .Q1(out_5[1]), .Q0(out_5[0]),
    .D0(multiplexer_1_out[0]), .LIN(xor_1_out), .S1(and_1_out), .S0(1'b1));
  SHRG4U shrg4u_2 (
    .CLK(in_1), .CLR_L(CLR_L), .RIN(and_1_out), .Q3(out_5[7]), .Q2(out_5[6]), .D3(multiplexer_1_out[7]),
    .D2(multiplexer_1_out[6]), .D1(multiplexer_1_out[5]), .Q1(out_5[5]), .Q0(out_5[4]),
    .D0(multiplexer_1_out[4]), .LIN(out_5[3]), .S1(and_1_out), .S0(1'b1));
  ExactlyOne xor_1 (.out(xor_1_out), .in0(out_5[7]), .in1(out_5[6]), .in2(out_5[5]), .in3(out_5[4]));

  // Other names for the same wires on the sheet: CLK = in_1; D[7:0] = in_3; LOAD = in_4; out[7:0] = out_5
endmodule
