// Logisim project lab3.5.circ as structural Verilog: 1 circuit, main circuit main
module main (
  input  CLK,
  input  LD,
  input  [3:0] HH1,
  input  [3:0] HH0,
  input  [3:0] MM1,
  input  [3:0] MM0,
  input  [3:0] SS1,
  input  [3:0] SS0,
  output [3:0] HH_H,
  output [3:0] HH_L,
  output [3:0] MM_H,
  output [3:0] MM_L,
  output [3:0] SS_H,
  output [3:0] SS_L,
  output LED_R,
  output LED_G,
  output LED_B,
  output INErr
);

  wire and_1_out, and_2_out, and_3_out, and_4_out, and_5_out, and_6_out, and_7_out, and_8_out, and_11_out,
       and_13_out, and_14_out, and_17_out, cntr4u_1_p8, cntr4u_1_p14, cntr4u_4_p8, cntr4u_6_p3,
       comparator_1_lt, comparator_2_lt, comparator_3_lt, comparator_4_lt, comparator_5_lt, comparator_6_lt,
       comparator_7_lt, comparator_8_eq, comparator_9_eq, comparator_9_lt, LED_EN, not_1_out, not_2_out,
       not_3_out, not_4_out, not_5_out, not_6_out, or_1_out, or_2_out, START, STOP;
  wire [3:0] cntr4u_3_p10, multiplexer_1_out;

  and and_1 (and_1_out, LD, ~INErr);  // AND_Gate
  and and_2 (and_2_out, LD, ~INErr);  // AND_Gate
  or or_1 (or_1_out, and_3_out, and_4_out);
  Comparator #(.width(4), .mode("unsigned")) comparator_1 (.a(HH1), .b(4'b0011), .lt(comparator_1_lt));  // open: gt, eq
  Comparator #(.width(4), .mode("unsigned")) comparator_2 (.a(HH0), .b(4'b0100), .lt(comparator_2_lt));  // open: gt, eq
  Comparator #(.width(4), .mode("unsigned")) comparator_3 (.a(HH0), .b(4'b1010), .lt(comparator_3_lt));  // open: gt, eq
  Comparator #(.width(4), .mode("unsigned")) comparator_4 (.a(MM1), .b(4'b0110), .lt(comparator_4_lt));  // open: gt, eq
  Comparator #(.width(4), .mode("unsigned")) comparator_5 (.a(MM0), .b(4'b1010), .lt(comparator_5_lt));  // open: gt, eq
  Comparator #(.width(4), .mode("unsigned")) comparator_6 (.a(SS1), .b(4'b0110), .lt(comparator_6_lt));  // open: gt, eq
  Comparator #(.width(4), .mode("unsigned")) comparator_7 (.a(SS0), .b(4'b1010), .lt(comparator_7_lt));  // open: gt, eq
  // CNTR4U cntr4u_1: pin names not known; wires that end beside it: CLK, and_1_out, or_1_out, HH0[0], HH0[1], HH0[2], HH0[3], cntr4u_1_p8, cntr4u_1_p8, HH_L[0], HH_L[1], HH_L[2], HH_L[3], cntr4u_1_p14
  and and_3 (and_3_out, HH_L[0], cntr4u_1_p8, HH_L[3]);
  and and_4 (and_4_out, HH_L[0], HH_L[1], HH_H[1], cntr4u_1_p8);
  // CNTR4U cntr4u_2: pin names not known; wires that end beside it: CLK, and_2_out, and_4_out, HH1[0], HH1[1], HH1[2], HH1[3], and_3_out, and_3_out, HH_H[0], HH_H[1], HH_H[2], HH_H[3]
  not not_1 (not_1_out, comparator_3_lt);
  not not_2 (not_2_out, comparator_4_lt);
  not not_3 (not_3_out, comparator_5_lt);
  not not_4 (not_4_out, comparator_6_lt);
  not not_5 (not_5_out, comparator_7_lt);
  // CNTR4U cntr4u_3: pin names not known; wires that end beside it: CLK, LED_EN, STOP, 1'b1, 1'b0, 1'b0, 1'b0, START, START, cntr4u_3_p10[0], cntr4u_3_p10[1], cntr4u_3_p10[2], cntr4u_3_p10[3]
  Multiplexer #(.width(4), .enable("false")) multiplexer_1 (
    .in0(4'b0000), .in1(cntr4u_3_p10), .out(multiplexer_1_out), .sel(START));
  Hex_Digit_Display hex_digit_display_1 (.value(HH_H));  // open: dp
  and and_5 (and_5_out, comparator_1_lt, comparator_2_lt);
  not not_6 (not_6_out, and_5_out);
  Hex_Digit_Display hex_digit_display_2 (.value(MM_H));  // open: dp
  Hex_Digit_Display hex_digit_display_3 (.value(HH_L), .dp(1'b1));
  xor xor_1 (LED_R, multiplexer_1_out[0], multiplexer_1_out[1]);
  xor xor_2 (LED_G, multiplexer_1_out[1], multiplexer_1_out[2]);
  xor xor_3 (LED_B, multiplexer_1_out[2], 1'b0);
  Hex_Digit_Display hex_digit_display_4 (.value(MM_L), .dp(1'b1));
  Hex_Digit_Display hex_digit_display_5 (.value(SS_H));  // open: dp
  and and_6 (and_6_out, LD, ~INErr);  // AND_Gate
  and and_7 (and_7_out, LD, ~INErr);  // AND_Gate
  or or_2 (or_2_out, not_6_out, not_1_out, not_2_out, not_3_out, not_4_out, not_5_out);
  Hex_Digit_Display hex_digit_display_6 (.value(SS_L), .dp(1'b1));
  and and_8 (and_8_out, MM_L[0], cntr4u_4_p8, MM_L[3]);
  and and_9 (cntr4u_1_p8, and_8_out, MM_H[2], MM_H[0], cntr4u_4_p8);
  and and_10 (INErr, or_2_out, LD);
  not not_7 (START, comparator_8_eq);
  Comparator #(.width(4), .mode("unsigned")) comparator_8 (
    .a(4'b0000), .b(cntr4u_3_p10), .eq(comparator_8_eq));  // open: gt, lt
  or or_3 (STOP, comparator_9_eq, comparator_9_lt);
  Comparator #(.width(4), .mode("unsigned")) comparator_9 (
    .a(4'b1010), .b(cntr4u_3_p10), .eq(comparator_9_eq), .lt(comparator_9_lt));  // open: gt
  // CNTR4U cntr4u_4: pin names not known; wires that end beside it: CLK, and_6_out, and_8_out, MM0[0], MM0[1], MM0[2], MM0[3], cntr4u_4_p8, cntr4u_4_p8, MM_L[0], MM_L[1], MM_L[2], MM_L[3]
  // CNTR4U cntr4u_5: pin names not known; wires that end beside it: CLK, and_7_out, cntr4u_1_p8, MM1[0], MM1[1], MM1[2], MM1[3], and_8_out, and_8_out, MM_H[0], MM_H[1], MM_H[2], MM_H[3]
  and and_11 (and_11_out, MM_L[0], MM_L[3], MM_H[2], MM_H[0]);
  // RGBLed RGBLED: pin names not known; wires that end beside it: LED_R, LED_G, LED_B
  and and_12 (LED_EN, and_11_out, and_17_out);
  and and_13 (and_13_out, LD, ~INErr);  // AND_Gate
  and and_14 (and_14_out, LD, ~INErr);  // AND_Gate
  // CNTR4U cntr4u_6: pin names not known; wires that end beside it: CLK, and_13_out, cntr4u_6_p3, SS0[0], SS0[1], SS0[2], SS0[3], 1'b1, 1'b1, SS_L[0], SS_L[1], SS_L[2], SS_L[3]
  and and_15 (cntr4u_6_p3, SS_L[0], SS_L[3]);
  and and_16 (cntr4u_4_p8, cntr4u_6_p3, SS_H[2], SS_H[0]);
  // CNTR4U cntr4u_7: pin names not known; wires that end beside it: CLK, and_14_out, cntr4u_4_p8, SS1[0], SS1[1], SS1[2], SS1[3], cntr4u_6_p3, cntr4u_6_p3, SS_H[0], SS_H[1], SS_H[2], SS_H[3]
  and and_17 (and_17_out, SS_H[2], SS_H[0], SS_L[3], SS_L[0]);

  // Other names for the same wires on the sheet: H0[3:0] = HH_L; H1[3:0] = HH_H; M0[3:0] = MM_L; M1[3:0] = MM_H;
  //   S0[3:0] = SS_L; S1[3:0] = SS_H

  // Notes on the sheet:
  //   设置初始时间BCD码
  //   输入信号
  //   请勿修改引脚名称、电路名称及电路封装外观
  //   数字时钟
  //   提示：使用4位二进制加法计数器子电路、比较器和独立逻辑门组件实现数字时钟。
  //   在载入有效时，检测设置数据错误
  //   生成三色LED显示信号，持续10个时钟周期
endmodule
