// Logisim project lab5.2.circ as structural Verilog: 1 circuit, main circuit DataRam
// DataRAM
module DataRam (
  input  CLK,
  input  CLR,
  input  WE,
  input  [2:0] MemOp,
  input  [17:0] Addr,
  input  [31:0] Din,
  output AlignErr,
  output [31:0] DataOut
);

  wire and_1_out, and_2_out, and_3_out, and_4_out, and_5_out, and_6_out, and_7_out, and_8_out, and_9_out,
       and_10_out, and_11_out, and_12_out, and_13_out, and_14_out, and_15_out, and_16_out, and_17_out,
       and_18_out, nand_1_out, SEL0, SEL1, SEL2, SEL3;
  wire [7:0] D1, D2, D3, D4, Dout0, Dout1, Dout2, Dout3, Ram0, Ram1, Ram2, Ram3;
  wire [31:0] bit_extender_1_out, bit_extender_2_out, bit_extender_3_out, bit_extender_4_out;

  RAM #(.addrWidth(16), .bus("separate"), .Select("high")) ram_1 (
    .addr(Addr[17:2]), .din(D1), .data(Ram3), .str(WE), .sel(SEL3), .clk(CLK), .clr(CLR));  // open: ld
  and and_1 (and_1_out, ~MemOp[0], ~MemOp[1]);  // AND_Gate
  and and_2 (and_2_out, and_1_out, nand_1_out);
  nand nand_1 (nand_1_out, ~Addr[0], ~Addr[1]);  // NAND_Gate
  and and_3 (and_3_out, ~MemOp[0], MemOp[1], Addr[0], ~Addr[1]);  // AND_Gate
  and and_4 (and_4_out, MemOp[1], ~MemOp[0], Addr[0], Addr[1]);  // AND_Gate
  and and_5 (and_5_out, MemOp[1], MemOp[0]);
  and and_6 (and_6_out, ~MemOp[0], ~MemOp[1], MemOp[2], ~Addr[1], ~Addr[0]);  // AND_Gate
  and and_7 (and_7_out, ~Addr[1], ~Addr[0], ~MemOp[1], ~MemOp[0]);  // AND_Gate
  and and_8 (and_8_out, ~MemOp[1], MemOp[0], Addr[1], Addr[0]);  // AND_Gate
  and and_9 (and_9_out, MemOp[1], ~MemOp[0], Addr[1], ~Addr[0]);  // AND_Gate
  or or_1 (AlignErr, and_2_out, and_3_out, and_6_out, and_4_out, and_5_out);
  or or_2 (SEL3, and_7_out, and_8_out, and_9_out);
  RAM #(.addrWidth(16), .bus("separate"), .Select("high")) ram_2 (
    .addr(Addr[17:2]), .din(D2), .data(Ram2), .str(WE), .sel(SEL2), .clk(CLK), .clr(CLR));  // open: ld
  RAM #(.addrWidth(16), .bus("separate"), .Select("high")) ram_3 (
    .addr(Addr[17:2]), .din(D3), .data(Ram1), .str(WE), .sel(SEL1), .clk(CLK), .clr(CLR));  // open: ld
  and and_10 (and_10_out, ~MemOp[1], ~MemOp[0], ~Addr[1], ~Addr[0]);  // AND_Gate
  and and_11 (and_11_out, ~MemOp[1], MemOp[0], ~Addr[1], Addr[0]);  // AND_Gate
  and and_12 (and_12_out, MemOp[1], ~MemOp[0], ~Addr[1], ~Addr[0]);  // AND_Gate
  and and_13 (and_13_out, ~MemOp[1], ~MemOp[0], ~Addr[1], ~Addr[0]);  // AND_Gate
  and and_14 (and_14_out, ~MemOp[1], MemOp[0], ~Addr[1], ~Addr[0]);  // AND_Gate
  and and_15 (and_15_out, ~Addr[1], ~Addr[0], ~MemOp[1], ~MemOp[0]);  // AND_Gate
  and and_16 (and_16_out, MemOp[1], ~MemOp[0], Addr[1], ~Addr[0]);  // AND_Gate
  and and_17 (and_17_out, ~MemOp[1], MemOp[0], Addr[1], ~Addr[0]);  // AND_Gate
  or or_3 (SEL1, and_10_out, and_11_out, and_12_out);
  and and_18 (and_18_out, MemOp[1], ~MemOp[0], ~Addr[1], ~Addr[0]);  // AND_Gate
  RAM #(.addrWidth(16), .bus("separate"), .Select("high")) ram_4 (
    .addr(Addr[17:2]), .din(D4), .data(Ram0), .str(WE), .sel(SEL0), .clk(CLK), .clr(CLR));  // open: ld
  or or_4 (SEL0, and_13_out, and_14_out, and_18_out);
  or or_5 (SEL2, and_15_out, and_16_out, and_17_out);
  assign bit_extender_1_out = {{24{1'b0}}, Dout0};  // Bit_Extender bit_extender_1
  assign bit_extender_2_out = {{16{1'b0}}, {Dout1, Dout0}};  // Bit_Extender bit_extender_2
  assign bit_extender_3_out = {{24{Dout0[7]}}, Dout0};  // Bit_Extender bit_extender_3
  assign bit_extender_4_out = {{16{Dout1[7]}}, {Dout1, Dout0}};  // Bit_Extender bit_extender_4
  Multiplexer #(.select(4), .width(8), .enable("false")) multiplexer_1 (
    .in0({8{1'b0}}), .in1({8{1'b0}}), .in2({8{1'b0}}), .in3({8{1'b0}}), .in4({8{1'b0}}), .in5({8{1'b0}}),
    .in6({8{1'b0}}), .in7({8{1'b0}}), .in8(Din[7:0]), .in9({8{1'b0}}), .in10({8{1'b0}}), .in11({8{1'b0}}),
    .in12(Din[15:8]), .in13({8{1'b0}}), .in14({8{1'b0}}), .in15(Din[31:24]), .out(D1),
    .sel({SEL3, SEL2, SEL1, SEL0}));
  Multiplexer #(.select(4), .width(8), .enable("false")) multiplexer_2 (
    .in0({8{1'b0}}), .in1({8{1'b0}}), .in2({8{1'b0}}), .in3({8{1'b0}}), .in4(Din[7:0]), .in5({8{1'b0}}),
    .in6({8{1'b0}}), .in7({8{1'b0}}), .in8({8{1'b0}}), .in9({8{1'b0}}), .in10({8{1'b0}}), .in11({8{1'b0}}),
    .in12(Din[7:0]), .in13({8{1'b0}}), .in14({8{1'b0}}), .in15(Din[23:16]), .out(D2),
    .sel({SEL3, SEL2, SEL1, SEL0}));
  Multiplexer #(.select(4), .width(8), .enable("false")) multiplexer_3 (
    .in0({8{1'b0}}), .in1({8{1'b0}}), .in2(Din[7:0]), .in3(Din[15:8]), .in4({8{1'b0}}), .in5({8{1'b0}}),
    .in6({8{1'b0}}), .in7({8{1'b0}}), .in8({8{1'b0}}), .in9({8{1'b0}}), .in10({8{1'b0}}), .in11({8{1'b0}}),
    .in12({8{1'b0}}), .in13({8{1'b0}}), .in14({8{1'b0}}), .in15(Din[15:8]), .out(D3),
    .sel({SEL3, SEL2, SEL1, SEL0}));
  Multiplexer #(.select(4), .width(8), .enable("false")) multiplexer_4 (
    .in0({8{1'b0}}), .in1(Din[7:0]), .in2({8{1'b0}}), .in3(Din[7:0]), .in4({8{1'b0}}), .in5({8{1'b0}}),
    .in6({8{1'b0}}), .in7({8{1'b0}}), .in8({8{1'b0}}), .in9({8{1'b0}}), .in10({8{1'b0}}), .in11({8{1'b0}}),
    .in12({8{1'b0}}), .in13({8{1'b0}}), .in14({8{1'b0}}), .in15(Din[7:0]), .out(D4),
    .sel({SEL3, SEL2, SEL1, SEL0}));
  Multiplexer #(.select(3), .width(32), .enable("false")) multiplexer_5 (
    .in0({Dout3, Dout2, Dout1, Dout0}), .in1(bit_extender_1_out), .in2(bit_extender_2_out),
    .in5(bit_extender_3_out), .in6(bit_extender_4_out), .out(DataOut), .sel(MemOp));  // open: in3, in4, in7
  Multiplexer #(.select(4), .width(8), .enable("false")) multiplexer_6 (
    .in1(Ram0), .in2(Ram1), .in3(Ram0), .in4(Ram2), .in8(Ram3), .in12(Ram2), .in15(Ram0), .out(Dout0),
    .sel({SEL3, SEL2, SEL1, SEL0}));  // open: in0, in5, in6, in7, in9, in10, in11, in13, in14
  Multiplexer #(.select(4), .width(8), .enable("false")) multiplexer_7 (
    .in3(Ram1), .in12(Ram3), .in15(Ram1), .out(Dout1), .sel({SEL3, SEL2, SEL1, SEL0}));  // open: in0, in1, in2, in4, in5, in6, in7, in8, in9, in10, in11, in13, in14
  Multiplexer #(.select(4), .width(8), .enable("false")) multiplexer_8 (
    .in15(Ram2), .out(Dout2), .sel({SEL3, SEL2, SEL1, SEL0}));  // open: in0, in1, in2, in3, in4, in5, in6, in7, in8, in9, in10, in11, in12, in13, in14
  Multiplexer #(.select(4), .width(8), .enable("false")) multiplexer_9 (
    .in15(Ram3), .out(Dout3), .sel({SEL3, SEL2, SEL1, SEL0}));  // open: in0, in1, in2, in3, in4, in5, in6, in7, in8, in9, in10, in11, in12, in13, in14

  // Other names for the same wires on the sheet: Dout[31:0] = DataOut

  // Notes on the sheet:
  //   输入引脚
  //   请勿修改引脚名称、电路名称及电路封装外观
  //   为了后续实验中的引用，不要修改MemOp的编码定义、引脚名称和在布局中的位置。
  //   输出引脚
endmodule
