// Logisim project lab4.1.circ as structural Verilog: 4 circuits, main circuit CLA4
module CLA4 (
  input  [3:0] X,
  input  [3:0] Y,
  input  Cin,
  output [3:0] F,
  output Cout,
  output Pg,
  output Gg
);

  wire clu4_1_c1, clu4_1_c2, clu4_1_c3, fa_1_g, fa_1_p, fa_2_g, fa_2_p, fa_3_g, fa_3_p, fa_4_g, fa_4_p;

  Hex_Digit_Display hex_digit_display_1 (.value(X));  // open: dp
  FA fa_1 (.A(X[3]), .F(F[3]), .B(Y[3]), .P(fa_1_p), .Cin(clu4_1_c3), .G(fa_1_g));
  Hex_Digit_Display hex_digit_display_2 (.value(Y));  // open: dp
  FA fa_2 (.A(X[1]), .F(F[1]), .B(Y[1]), .P(fa_2_p), .Cin(clu4_1_c1), .G(fa_2_g));
  FA fa_3 (.A(X[2]), .F(F[2]), .B(Y[2]), .P(fa_3_p), .Cin(clu4_1_c2), .G(fa_3_g));
  Hex_Digit_Display hex_digit_display_3 (.value(F));  // open: dp
  CLU4 clu4_1 (
    .P0(fa_4_p), .P1(fa_2_p), .P2(fa_3_p), .P3(fa_1_p), .C1(clu4_1_c1), .C3(clu4_1_c3), .G0(fa_4_g),
    .G1(fa_2_g), .G2(fa_3_g), .G3(fa_1_g), .C2(clu4_1_c2), .C4(Cout), .C0(Cin), .Pg(Pg), .Gg(Gg));
  FA fa_4 (.A(X[0]), .F(F[0]), .B(Y[0]), .P(fa_4_p), .Cin(Cin), .G(fa_4_g));

  // Other names for the same wires on the sheet: Z[3:0] = F

  // Notes on the sheet:
  //   +
  //   =
  //   输出
  //   输入
  //   请勿修改引脚名称、电路名称及电路封装外观
  //   提示：使用全加器和CLU子电路实现四位先行进位加法器CLA4
endmodule

module CLU4 (
  input  P0,
  input  P1,
  input  P2,
  input  P3,
  input  G0,
  input  G1,
  input  G2,
  input  G3,
  input  C0,
  output C1,
  output C3,
  output C2,
  output C4,
  output Pg,
  output Gg
);

  wire and_1_out, and_2_out, and_3_out, and_4_out, and_5_out, and_6_out, and_7_out, and_8_out, and_9_out,
       and_10_out, and_11_out, and_12_out, and_13_out;

  and and_1 (and_1_out, P3, G2);
  and and_2 (and_2_out, P3, P2, G1);
  or or_1 (C4, G3, and_1_out, and_2_out, and_3_out, and_4_out);
  and and_3 (and_3_out, P3, P2, P1, G0);
  and and_4 (and_4_out, P3, P2, P1, P0, C0);
  and and_5 (and_5_out, P2, G1);
  or or_2 (C3, G2, and_5_out, and_7_out, and_6_out);
  and and_6 (and_6_out, P2, P1, P0, C0);
  and and_7 (and_7_out, P2, P1, G0);
  and and_8 (and_8_out, P3, G2);
  or or_3 (Gg, G3, and_8_out, and_10_out, and_12_out);
  and and_9 (and_9_out, P1, G0);
  and and_10 (and_10_out, P3, P2, G1);
  or or_4 (C2, G1, and_9_out, and_11_out);
  and and_11 (and_11_out, P1, P0, C0);
  and and_12 (and_12_out, P3, P2, P1, G0);
  or or_5 (C1, G0, and_13_out);
  and and_13 (and_13_out, P0, C0);
  and and_14 (Pg, P0, P1, P2, P3);

  // Notes on the sheet:
  //   输入引脚
  //   请勿修改引脚名称、电路名称及电路封装外观
  //   提示：使用逻辑门电路实现4位四位先行进位部件CLU，Pg、Gg为成组进位生成传递函数
  //   输出引脚
endmodule

module FA (
  input  A,
  input  B,
  input  Cin,
  output F,
  output P,
  output G
);

  wire xor_1_out;

  or or_1 (P, A, B);
  and and_1 (G, A, B);
  xor xor_1 (xor_1_out, A, B);
  xor xor_2 (F, xor_1_out, Cin);

  // Notes on the sheet:
  //   全加器
  //   输入引脚
  //   请勿修改引脚名称、电路名称及电路封装外观
  //   使用2输入异或门级联生成求和F，不要使用3输入异或门
  //   输出引脚
endmodule

module \测试CLA  (
  input  [3:0] X,
  input  [3:0] Y,
  input  C0,
  output [3:0] S,
  output C4,
  output C3,
  output G_star,
  output P_star
);

  CLA4 \_4位CLA  (.X(X), .F(S), .Cout(C4), .Y(Y), .Pg(P_star), .Cin(C0), .Gg(G_star));
  // Probe on X
  // Probe on Y
  // Probe on S
  // Probe on X
  // Probe on Y
  // Probe on S

  // Notes on the sheet:
  //   X: pull=down
  //   C0: pull=down
  //   Y: pull=down
  //   输入引脚区
  //   4位快速加法器
  //   输出引脚区
  //   功能说明:4位Adder  S=X+Y，C4、C3分别为最高位、次高位进位位，C0为进位输入， G* P*为成组进位生成传递函数
  //   +
  //   =
  //   有符号加法
  //   +
  //   =
  //   无符号加法
endmodule
