// Logisim project 1-1CMOS-not.circ as structural Verilog: 1 circuit, main circuit cmos_not
module cmos_not (
  input  x,
  output z
);

  not not_1 (z, x);

  // Notes on the sheet:
  //   输入引脚
  //   请勿增加、删除引脚，用隧道标签构建电路
  //   请勿更改电路封装外观
  //   非门实现电路
  //   输出引脚
  //   大连外国语大学数字逻辑与计算机组成课程组
endmodule
