// Logisim project 1-2BoolExpr.circ as structural Verilog: 1 circuit, main circuit 布尔表达式
// Bool
module \布尔表达式  (
  input  A,
  input  B,
  input  C,
  output F
);

  wire nand_1_out, nand_2_out, nand_3_out, nand_4_out, nand_5_out;

  nand nand_1 (nand_1_out, B, C);
  nand nand_2 (nand_2_out, A, C);
  nand nand_3 (nand_3_out, nand_1_out, nand_2_out);
  nand nand_4 (nand_4_out, nand_3_out, nand_3_out);
  nand nand_5 (nand_5_out, A, B);
  nand nand_6 (F, nand_4_out, nand_5_out);
endmodule
