// Logisim project 1-4ReducedTable.circ as structural Verilog: 1 circuit, main circuit 简化真值表
// sTruth
module \简化真值表  (
  input  X1,
  input  X0,
  input  Y1,
  input  Y0,
  output Gt
);

  wire nand_1_out, nand_2_out, nand_3_out, nand_4_out, nand_5_out, nand_6_out, nand_7_out, nand_8_out,
       nand_9_out, nand_10_out, nand_11_out, nand_12_out, nand_13_out, nand_14_out, nand_15_out, nand_16_out,
       nand_17_out, nand_18_out;

  nand nand_1 (nand_1_out, Y0, Y0);
  nand nand_2 (nand_2_out, X1, X0);
  nand nand_3 (nand_3_out, Y1, nand_1_out);
  nand nand_4 (nand_4_out, Y1, Y1);
  nand nand_5 (nand_5_out, nand_2_out, nand_2_out);
  nand nand_6 (nand_6_out, nand_3_out, nand_3_out);
  nand nand_7 (nand_7_out, X1, X1);
  nand nand_8 (nand_8_out, Y1, Y1);
  nand nand_9 (nand_9_out, Y0, Y0);
  nand nand_10 (nand_10_out, X1, nand_4_out);
  nand nand_11 (nand_11_out, nand_5_out, nand_6_out);
  nand nand_12 (nand_12_out, nand_7_out, X0);
  nand nand_13 (nand_13_out, nand_8_out, nand_9_out);
  nand nand_14 (nand_14_out, nand_10_out, nand_11_out);
  nand nand_15 (nand_15_out, nand_12_out, nand_12_out);
  nand nand_16 (nand_16_out, nand_13_out, nand_13_out);
  nand nand_17 (nand_17_out, nand_14_out, nand_14_out);
  nand nand_18 (nand_18_out, nand_15_out, nand_16_out);
  nand nand_19 (Gt, nand_17_out, nand_18_out);
endmodule
