// Logisim project ReducedTableTest.circ as structural Verilog: 2 circuits, main circuit 简化真值表测试
module \简化真值表测试  (
  output [3:0] Cnt,
  output [1:0] X,
  output [1:0] Y,
  output Gt,
  output _passed,
  output halt
);

  wire CLK, GtS, Run;

  Clock #(.highDuration(1), .lowDuration(1)) clock_1 (.out(CLK));
  Counter #(.width(4), .max('hf), .ongoal("wrap"), .trigger("rising"), .behavior("old")) counter_1 (
    .count(Run), .Q(Cnt), .clk(CLK));  // open: load, D, carry, clr, preset
  // Probe on Cnt
  // Probe on 4'b1111
  // Probe on Cnt
  Comparator #(.width(4), .mode("twosComplement")) comparator_1 (.a(Cnt), .b(4'b1111), .eq(halt));  // open: gt, lt
  ROM #(.addrWidth(4), .dataWidth(4), .Select("high")) rom_1 (.addr(Cnt), .data({X, Y}));
  ROM #(.addrWidth(4), .dataWidth(1), .Select("high")) rom_2 (.addr(Cnt), .data(GtS));
  not not_1 (Run, halt);
  \简化真值表  \u_简化真值表_1  (.X1(X[1]), .X0(X[0]), .Y1(Y[1]), .Y0(Y[0]), .Gt(Gt));
  RAM #(.addrWidth(4), .dataWidth(1), .bus("separate"), .Select("low")) ram_1 (
    .addr(Cnt), .din(Gt), .str(Run), .clk(CLK));  // open: data, sel, ld, clr
  Comparator #(.width(1), .mode("twosComplement")) comparator_2 (.a(Gt), .b(GtS), .eq(_passed));  // open: gt, lt
  Pull_Resistor #(.pull(0)) pull_resistor_1 (.node(_passed));

  // Other names for the same wires on the sheet: Equal = _passed; tunnel[3:0] = Cnt

  // Notes on the sheet:
  //   测试节拍数
  //   contents of rom_1 (hex, n*v repeats v):
  //   0 1 2 3 4 5 6 7 8 9 a b c d e f
  //   contents of rom_2 (hex, n*v repeats v):
  //   4*0 1 0 0 0 1 1 0 0 1 1 1
endmodule

module MEM (
);

  wire CLK, nHalt;
  wire [4:0] mAddr;
  wire [7:0] tunnel;

  RAM #(.addrWidth(8), .dataWidth(5), .bus("separate"), .Select("low")) ram_1 (
    .addr(tunnel), .din(mAddr), .str(nHalt), .clk(CLK));  // open: data, sel, ld, clr
endmodule
